# Fritzing sketch sketch (saved by Fritzing 0.9.3b)
breadboards: 2

parts:
  U1 = ESP32-38PinWide [part_number=ESP32-38PinWide]
  Part3 = Real Time Clock Module - DS1307 RTC Breakout Board
  S1 = PH meter [package=THT]
  Part4 = LCD1602-I2C
  Part5 = Jtron 1 Channel Optoisolated Relay Module [package=relay]
  S2 = Momentary Switch [package=ksa_sealed_tac_switch]
  S3 = Momentary Switch [package=ksa_sealed_tac_switch]
  S4 = Momentary Switch [package=ksa_sealed_tac_switch]
  S5 = Momentary Switch [package=ksa_sealed_tac_switch]
  R1 = Resistor [tolerance=±5% resistance=1k package="0805 [SMD]"]
  Q1 = NPN-Transistor [package="TO92 [THT]"]
  C1 = Electrolytic Capacitor [capacitance=1000µF package="300 mil [THT, electrolytic]"]
  R2 = Resistor [tolerance=±5% resistance=1k package="0805 [SMD]"]
  R3 = Resistor [tolerance=±5% resistance=1k package="0805 [SMD]"]
  R4 = Resistor [tolerance=±5% resistance=1k package="0805 [SMD]"]
  R5 = Resistor [tolerance=±5% resistance=1k package="0805 [SMD]"]
  Water_Level_Sensor1 = Water Level Sensor
  Part6 = Bluetooth HC-05 Macho
  R6 = Resistor [tolerance=±5% resistance=1k package="0805 [SMD]"]
  R7 = Resistor [tolerance=±5% resistance=1k package="0805 [SMD]"]

nets:
  N1: U1.GPIO36, Water_Level_Sensor1.SIG
  N2: U1.GPIO39, R7.Pin_1
  N3: U1.GPIO34, S5.1, S5.2, R3.Pin_1
  N4: U1.GPIO35, S2.1, S2.2, R2.Pin_1
  GND: U1.GPIO11, Part4.GND, S2.3, S2.4, S3.3, S3.4, S4.3, S4.4, S5.3, S5.4, Water_Level_Sensor1.GND, Part6.GND
  VCC: U1.VIN, Part3.5V, S1.pin2, Part4.VCC, Part5.VCC, R1.Pin_0, C1.+, Water_Level_Sensor1.VCC, Part6.VCC
  N5: U1.GPIO2, Q1.B
  N6: U1.GPIO16, Part6.TXD
  N7: U1.GPIO17, Part6.RXD
  N8: U1.GPIO18, S3.1, S3.2, R5.Pin_1
  N9: U1.GPIO19, S4.1, S4.2, R4.Pin_1
  N10: U1.GPIO21, Part3.SDA, Part4.SDA
  N11: U1.GPIO22, Part3.SCL, Part4.SCL
  GND_2: Part3.GND, S1.pin1, Part5.GND, Q1.C, C1.-, R6.Pin_0
  N12: S1.pin3, R6.Pin_1, R7.Pin_0
  N13: Part5.IN1, R1.Pin_1, Q1.E
  N14: R2.Pin_0, R3.Pin_0, R4.Pin_0, R5.Pin_0

custom parts:
  ESP32-38PinWide: Generic 38-Pin ESP32 with wide format (only access to one side of pins on a breadboard) based on Stephen Lilley's HiLetgo ESP-WROOM-32 ESP32 ESP-32S Development Board.
  LCD1602-I2C: A standard character display, usually with 2x16 characters. Comes in many colors with LCM1602 IIC attached.
  Water Level Sensor: A water level sensor. This sensor operates at 3V to 5V. The Sig (signal) pin outputs an analogue signal that is in proportion to the amount of water in contact with the sensor.
